# Fritzing sketch ESP8266_starter (saved by Fritzing 0.9.3b)
breadboards: 1

parts:
  U1 = ESP8266 WiFi Module [part_number=ESP8266]
  Componente1 = Arduino Mega 2560 (Rev3)

nets:
  N1: U1.RXD, Componente1.D16_PWM/TX2
  VCC: U1.VCC, U1.CH_PD, Componente1.3V3
  GND: U1.GND, Componente1.GND
  N2: U1.TXD, Componente1.D17_PWM/RX2

custom parts:
  ESP8266 WiFi Module: Generic WiFi Module based on the ESP8266 with onboard PCB antenna and UART communications
