# Fritzing sketch Keypad_Shield_Lcd (saved by Fritzing 0.9.3b)
breadboards: 1

parts:
  Componente1 = Adafruit RGB LCD Shield [part_number="Adafruit #714 and #716"]
  Componente2 = Arduino Mega 2560 (Rev3)

nets:
  +5V: Componente1.+5V, Componente2.5V
  N1: Componente1.D4, Componente2.D24
  N2: Componente1.D5, Componente2.D25
  N3: Componente1.D6, Componente2.D26
  N4: Componente1.D7, Componente2.D27
  N5: Componente1.D8, Componente2.D28
  N6: Componente1.D9, Componente2.D29
  GND: Componente1.GND, Componente2.GND

custom parts:
  Adafruit RGB LCD Shield: This new Adafruit shield makes it easy to use a 16x2 Character LCD. We really like the RGB LCDs we stock in the shop both the RGB negative and RGB positive. Unfortunately, these LCDs do require quite a few digital pins, 6 to control the LCD and then another 3 to control the RGB backlight for a total of 9 pins. That's half of the pins available on a classic Arduino! With this in mind, we wanted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
