# Fritzing sketch Servomotor (saved by Fritzing 0.9.3b)
breadboards: 1

parts:
  Componente1 = Arduino Mega 2560 (Rev3)
  J1 = Basic Servo

nets:
  N1: Componente1.D9_PWM, J1.pulse
  VIN: Componente1.VIN, J1.gnd
  5V: Componente1.5V, J1.vcc
