# Fritzing sketch Sistema_completo (saved by Fritzing 0.9.3b)
breadboards: 1

parts:
  Componente1 = Arduino Mega 2560 (Rev3)
  hc-sr1 = hc-sr04
  U2 = ESP8266 WiFi Module [part_number=ESP8266]
  Componente4 = Adafruit RGB LCD Shield [part_number="Adafruit #714 and #716"]
  Componente5 = RFID-RC522-v2
  J1 = Basic Servo

nets:
  N1: Componente1.D17_PWM/RX2, U2.TXD
  N2: Componente1.D16_PWM/TX2, U2.RXD
  N3: Componente1.D11_PWM, hc-sr1.Echo
  N4: Componente1.D9_PWM, J1.pulse
  5V: Componente1.5V, Componente4.+5V, Componente5.3.3V
  GND: Componente1.GND, Componente4.GND, Componente5.GND
  N5: Componente1.D3_PWM, hc-sr1.Trig
  N6: Componente1.D5_PWM, Componente5.RST
  N7: Componente1.D24, Componente1.D25, Componente4.D3, Componente4.D4, Componente4.D5
  N8: Componente1.D26, Componente4.D6
  N9: Componente1.D27, Componente4.D7
  N10: Componente1.D28, Componente4.D8
  N11: Componente1.D29, Componente4.D9
  N12: Componente1.D50, Componente5.MISO
  N13: Componente1.D51, Componente5.MOSI
  N14: Componente1.D52, Componente5.SCK
  N15: Componente1.D53, Componente5.SDA
  VCC: hc-sr1.VCC, J1.vcc
  GND_2: hc-sr1.GND, J1.gnd
  N16: U2.VCC, U2.CH_PD

custom parts:
  ESP8266 WiFi Module: Generic WiFi Module based on the ESP8266 with onboard PCB antenna and UART communications
  Adafruit RGB LCD Shield: This new Adafruit shield makes it easy to use a 16x2 Character LCD. We really like the RGB LCDs we stock in the shop both the RGB negative and RGB positive. Unfortunately, these LCDs do require quite a few digital pins, 6 to control the LCD and then another 3 to control the RGB backlight for a total of 9 pins. That's half of the pins available on a classic Arduino! With this in mind, we wanted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
  RFID-RC522-v2: A simple China made RFID-RC522 Reader; do check the pin labels, as this is a MFRC522 based clone.
